# Fritzing sketch FullColorLED_light (saved by Fritzing 0.9.1b)
breadboards: 1

parts:
  Raspberry_Pi1 = Raspberry Pi B+
  LED2 = RGB LED (com. cathode, rbg) [package="5 mm [THT]"]  # not connected
  LED3 = RGB LED (com. cathode, rbg) [package="5 mm [THT]"]
  LED4 = RGB LED (com. cathode, rbg) [package="5 mm [THT]"]
  LED5 = RGB LED (com. cathode, rbg) [package="5 mm [THT]"]
  LED6 = RGB LED (com. cathode, rbg) [package="5 mm [THT]"]
  S1 = Pushbutton [package="[THT]"]
  R2 = Resistor [tolerance=±5% resistance=150 package=THT]
  R3 = Resistor [tolerance=±5% resistance=150 package=THT]
  R4 = Resistor [tolerance=±5% resistance=150 package=THT]
  R5 = Resistor [tolerance=±5% resistance=150 package=THT]
  R6 = Resistor [tolerance=±5% resistance=240 package=THT]
  R7 = Resistor [tolerance=±5% resistance=240 package=THT]
  R8 = Resistor [tolerance=±5% resistance=240 package=THT]
  R9 = Resistor [tolerance=±5% resistance=240 package=THT]
  R1 = Resistor [tolerance=±5% resistance=100 package=THT]
  R10 = Resistor [tolerance=±5% resistance=100 package=THT]
  R11 = Resistor [tolerance=±5% resistance=100 package=THT]
  R12 = Resistor [tolerance=±5% resistance=100 package=THT]

nets:
  N1: Raspberry_Pi1.GPIO2, R2.Pin_1
  N2: Raspberry_Pi1.GPIO3, R6.Pin_1
  N3: Raspberry_Pi1.GPIO4, R10.Pin_1
  N4: Raspberry_Pi1.GND, LED3.common_cathode, LED4.common_cathode, LED5.common_cathode, LED6.common_cathode, S1.Pin_1, S1.Pin_2
  N5: Raspberry_Pi1.GPIO17, R3.Pin_1
  N6: Raspberry_Pi1.GPIO27, R7.Pin_1
  N7: Raspberry_Pi1.GPIO22, R11.Pin_1
  N8: Raspberry_Pi1.GPIO10, R4.Pin_1
  N9: Raspberry_Pi1.GPIO9, R8.Pin_1
  N10: Raspberry_Pi1.GPIO11, R12.Pin_1
  N11: Raspberry_Pi1.GPIO7, S1.Pin_3, S1.Pin_4
  N12: Raspberry_Pi1.GPIO25, R1.Pin_1
  N13: Raspberry_Pi1.GPIO24, R9.Pin_1
  N14: Raspberry_Pi1.GPIO23, R5.Pin_1
  N15: LED3.red_anode, R2.Pin_0
  N16: LED3.blue_anode, R10.Pin_0
  N17: LED3.green_anode, R6.Pin_0
  N18: LED4.red_anode, R3.Pin_0
  N19: LED4.blue_anode, R11.Pin_0
  N20: LED4.green_anode, R7.Pin_0
  N21: LED5.red_anode, R4.Pin_0
  N22: LED5.blue_anode, R12.Pin_0
  N23: LED5.green_anode, R8.Pin_0
  N24: LED6.red_anode, R5.Pin_0
  N25: LED6.blue_anode, R1.Pin_0
  N26: LED6.green_anode, R9.Pin_0
