# Fritzing sketch LED_light (saved by Fritzing 0.9.1b)
breadboards: 1

parts:
  Raspberry_Pi1 = Raspberry Pi B+
  R1 = Resistor [tolerance=±5% resistance=220 package=THT]
  LED1 = LED - 5mm [color="Red (633nm)" package="5 mm [THT]"]
  LED2 = LED - 5mm [color="Red (633nm)" package="5 mm [THT]"]  # not connected

nets:
  N1: Raspberry_Pi1.3v3, LED1.anode
  N2: Raspberry_Pi1.GND, R1.Pin_1
  N3: R1.Pin_0, LED1.cathode
